# Fritzing sketch schematic (saved by Fritzing 0.9.3b)
breadboards: 1

parts:
  Q1 = NPN-Transistor [package="TO92 [THT]"]
  R1 = Resistor [tolerance=±5% resistance=220 package=THT]
  U1 = NodeMCU V3.0
  DHT1 = DHT22 Humidity and Temperature Sensor
  Part1 = Soil Moisture Sensor
  U2 = mystery part, 5 pins [chip_label="pump 5v"]

nets:
  GND: Q1.E, U1.GND#6, U1.GND#13, U1.GND#16, U1.GND#33, DHT1.GND, Part1.GND
  N1: Q1.B, R1.Pin_0
  N2: Q1.C, U2.pin1
  N3: R1.Pin_1, U1.D3
  N4: U1.D0, DHT1.DATA
  VIN: U1.Vin, DHT1.VDD, Part1.VCC, U2.pin5
  N5: U1.A0, Part1.SIG

custom parts:
  NodeMCU V3.0: ESP8266 based NodeMCU
